// Digital circuit 4-bit_register.dig as structural Verilog
module _4_bit_register (
  input  [3:0] Data,
  input  C,
  output [3:0] Out
);

  _1_bit_memory_cell__D_flip_flop _1_bit_memory_cell__d_flip_flop_1 (.D(Data[0]), .C(C), .Q(Out[0]));
  _1_bit_memory_cell__D_flip_flop _1_bit_memory_cell__d_flip_flop_2 (.D(Data[1]), .C(C), .Q(Out[1]));
  _1_bit_memory_cell__D_flip_flop _1_bit_memory_cell__d_flip_flop_3 (.D(Data[2]), .C(C), .Q(Out[2]));
  _1_bit_memory_cell__D_flip_flop _1_bit_memory_cell__d_flip_flop_4 (.D(Data[3]), .C(C), .Q(Out[3]));
endmodule
