// Digital circuit 4bit_ALU.dlogic.dig as structural Verilog
module _4bit_ALU_dlogic (
  input  [3:0] A,
  input  [3:0] B,
  input  [2:0] Control,
  input  zero,
  output [3:0] Result,
  output Zero_Flag,
  output overflow,
  output Less_Than_Flag,
  output underflow
);

  wire not_1_out;
  wire [3:0] _4bit_full_adder_1_sum, _4bit_logicoperations_1_and_output, _4bit_logicoperations_1_or_output,
       _4bit_logicoperations_1_xor_output, _4bit_subtractor_1_difference;
  wire [4:0] _4bit_setlessthanflag_1_result;

  not not_1 (not_1_out, zero);
  _4bit_full_adder _4bit_full_adder_1 (.zero(zero), .A(A), .B(B), .sum(_4bit_full_adder_1_sum), .overflow(overflow));
  _4bit_subtractor _4bit_subtractor_1 (
    .A(A), .B(B), .CIN(not_1_out), .Difference(_4bit_subtractor_1_difference), .Underflow(underflow));
  _4bit_logicOperations _4bit_logicoperations_1 (
    .A(A), .B(B), .AND_Output(_4bit_logicoperations_1_and_output),
    .OR_Output(_4bit_logicoperations_1_or_output), .XOR_Output(_4bit_logicoperations_1_xor_output));
  _4bit_setLessThanFlag _4bit_setlessthanflag_1 (.A(A), .B(B), .zero(zero), .Result(_4bit_setlessthanflag_1_result));
  _4bit_multiplexer_6x2 _4bit_multiplexer_6x2_1 (
    .Control(Control), .ADD(_4bit_full_adder_1_sum), .SUB(_4bit_subtractor_1_difference),
    .AND(_4bit_logicoperations_1_and_output), .OR(_4bit_logicoperations_1_or_output),
    .XOR(_4bit_logicoperations_1_xor_output), .SLT(_4bit_setlessthanflag_1_result), .R(Result),
    .LT(Less_Than_Flag));
  _4bit_zeroflag _4bit_zeroflag_1 (.I(Result), .ZF(Zero_Flag));
  // Pins of 1 and 3 bits meet at Control
endmodule
