// Digital circuit 4bit_Instruction_Register.dig as structural Verilog
module _4bit_Instruction_Register (
  input  [3:0] Data,
  input  C,
  output [3:0] Address_Bus,
  output Out_of_Incrament
);

  wire decoder_1_out_0, decoder_1_out_2;
  wire [1:0] IR_p3;

  // _4_bit_register IR: pin names not known; wires that end beside it: Data, C, IR_p3, IR_p3
  Decoder #(.Selector_Bits(2)) decoder_1 (
    .sel(IR_p3), .out_0(decoder_1_out_0), .out_2(decoder_1_out_2));  // open: out_1, out_3
  // programCounter programcounter_1: pin names not known; wires that end beside it: decoder_1_out_0, decoder_1_out_2, Address_Bus, Out_of_Incrament
endmodule
