// Digital circuit 4bit_logicOperations.dig as structural Verilog
module _4bit_logicOperations (
  input  [3:0] A,
  input  [3:0] B,
  output [3:0] AND_Output,
  output [3:0] OR_Output,
  output [3:0] XOR_Output
);

  assign AND_Output = A & B;  // And and_1, 4 bits wide
  assign OR_Output = A | B;  // Or or_1, 4 bits wide
  assign XOR_Output = A ^ B;  // XOr xor_1, 4 bits wide
endmodule
