// Digital circuit 4bit_multiplexer(6x2).dig as structural Verilog
module _4bit_multiplexer_6x2 (
  input  [2:0] Control,
  input  [3:0] ADD,
  input  [3:0] SUB,
  input  [3:0] AND,
  input  [3:0] OR,
  input  [3:0] XOR,
  input  [4:0] SLT,
  output [3:0] R,
  output LT
);

  wire and_1_out, and_2_out, and_3_out, and_4_out, and_5_out, and_6_out, not_1_out, not_2_out, not_3_out,
       not_4_out, not_5_out, not_6_out, not_7_out, not_8_out, not_9_out, not_10_out, not_11_out;
  wire [3:0] and_7_out, and_11_out, and_15_out, and_19_out, and_23_out, and_27_out;

  not not_1 (not_1_out, Control[0]);
  not not_2 (not_2_out, Control[1]);
  not not_3 (not_3_out, Control[2]);
  not not_4 (not_4_out, Control[1]);
  not not_5 (not_5_out, Control[2]);
  not not_6 (not_6_out, Control[0]);
  not not_7 (not_7_out, Control[2]);
  not not_8 (not_8_out, Control[2]);
  not not_9 (not_9_out, Control[0]);
  not not_10 (not_10_out, Control[1]);
  not not_11 (not_11_out, Control[1]);
  and and_1 (and_1_out, not_1_out, not_2_out, not_3_out);
  and and_2 (and_2_out, Control[0], not_4_out, not_5_out);
  and and_3 (and_3_out, not_6_out, Control[1], not_7_out);
  and and_4 (and_4_out, Control[0], Control[1], not_8_out);
  and and_5 (and_5_out, not_9_out, not_10_out, Control[2]);
  and and_6 (and_6_out, Control[0], not_11_out, Control[2]);
  and and_7 (and_7_out[0], ADD[0], and_1_out);
  and and_8 (and_7_out[1], ADD[1], and_1_out);
  and and_9 (and_7_out[2], ADD[2], and_1_out);
  and and_10 (and_7_out[3], ADD[3], and_1_out);
  and and_11 (and_11_out[0], SUB[0], and_2_out);
  and and_12 (and_11_out[1], SUB[1], and_2_out);
  and and_13 (and_11_out[2], SUB[2], and_2_out);
  and and_14 (and_11_out[3], SUB[3], and_2_out);
  and and_15 (and_15_out[0], AND[0], and_3_out);
  and and_16 (and_15_out[1], AND[1], and_3_out);
  and and_17 (and_15_out[2], AND[2], and_3_out);
  and and_18 (and_15_out[3], AND[3], and_3_out);
  and and_19 (and_19_out[0], OR[0], and_4_out);
  and and_20 (and_19_out[1], OR[1], and_4_out);
  and and_21 (and_19_out[2], OR[2], and_4_out);
  and and_22 (and_19_out[3], OR[3], and_4_out);
  and and_23 (and_23_out[0], XOR[0], and_5_out);
  and and_24 (and_23_out[1], XOR[1], and_5_out);
  and and_25 (and_23_out[2], XOR[2], and_5_out);
  and and_26 (and_23_out[3], XOR[3], and_5_out);
  and and_27 (and_27_out[0], and_6_out, SLT[0]);
  and and_28 (and_27_out[1], and_6_out, SLT[1]);
  and and_29 (and_27_out[2], and_6_out, SLT[2]);
  and and_30 (and_27_out[3], and_6_out, SLT[3]);
  and and_31 (LT, and_6_out, SLT[4]);
  assign R = and_7_out ^ and_11_out ^ and_15_out ^ and_19_out ^ and_23_out ^ and_27_out;  // XOr xor_1, 4 bits wide
endmodule
