// Digital circuit 4bit_setLessThanFlag.dig as structural Verilog
module _4bit_setLessThanFlag (
  input  [3:0] A,
  input  [3:0] B,
  input  zero,
  output [4:0] Result
);

  wire and_2_out, and_3_out, and_5_out, and_6_out, and_8_out, and_9_out, and_10_out, not_1_out, not_2_out,
       not_3_out, not_4_out;

  not not_1 (not_1_out, A[3]);
  and and_1 (Result[4], not_1_out, B[3]);
  not not_2 (not_2_out, A[2]);
  and and_2 (and_2_out, A[3], B[3]);
  and and_3 (and_3_out, not_2_out, B[2]);
  and and_4 (Result[4], and_2_out, and_3_out);
  and and_5 (and_5_out, A[3], B[3], A[2], B[2]);
  not not_3 (not_3_out, A[1]);
  and and_6 (and_6_out, not_3_out, B[1]);
  and and_7 (Result[4], and_5_out, and_6_out);
  and and_8 (and_8_out, A[3], B[3], A[2], A[2]);
  and and_9 (and_9_out, A[1], B[1]);
  not not_4 (not_4_out, A[0]);
  and and_10 (and_10_out, not_4_out, B[0]);
  and and_11 (Result[4], and_8_out, and_9_out, and_10_out);

  assign Result[3:0] = {{3{zero}}, Result[4]};
endmodule
