// Digital circuit 4bit_subtractor.dig as structural Verilog
module _4bit_subtractor (
  input  [3:0] A,
  input  [3:0] B,
  input  CIN,
  output [3:0] Difference,
  output Underflow
);

  wire _1bit_full_adder_1_cout, _1bit_full_adder_2_cout, _1bit_full_adder_3_cout, not_1_out, not_2_out,
       not_3_out, not_4_out;

  not not_1 (not_1_out, B[0]);
  not not_2 (not_2_out, B[1]);
  not not_3 (not_3_out, B[2]);
  not not_4 (not_4_out, B[3]);
  _1bit_full_adder _1bit_full_adder_1 (
    .A(A[0]), .B(not_1_out), .Cin(CIN), .Sum(Difference[0]), .Cout(_1bit_full_adder_1_cout));
  _1bit_full_adder _1bit_full_adder_2 (
    .A(A[1]), .B(not_2_out), .Cin(_1bit_full_adder_1_cout), .Sum(Difference[1]),
    .Cout(_1bit_full_adder_2_cout));
  _1bit_full_adder _1bit_full_adder_3 (
    .A(A[2]), .B(not_3_out), .Cin(_1bit_full_adder_2_cout), .Sum(Difference[2]),
    .Cout(_1bit_full_adder_3_cout));
  _1bit_full_adder _1bit_full_adder_4 (
    .A(A[3]), .B(not_4_out), .Cin(_1bit_full_adder_3_cout), .Sum(Difference[3]), .Cout(Underflow));

  // Notes on the sheet:
  //   CIN: default 1
endmodule
