// Digital circuit complete_CPU.dig as structural Verilog
module complete_CPU (
);

  _4bit_ALU_dlogic _4bit_alu_dlogic_1 ();  // open: A, B, Control, zero, Result, Zero_Flag, overflow, Less_Than_Flag, underflow
endmodule
