// Digital circuit memory_Module.dig as structural Verilog
module memory_Module (
  input  [3:0] Address,
  input  [3:0] Data,
  input  Read,
  input  Write
);

  Register #(.Bits(4)) register_1 ();  // open: D, C, en, Q
endmodule
