// Digital circuit programCounter.dig as structural Verilog
module programCounter (
  input  [3:0] Load,
  input  Increment,
  output [3:0] Address_bus
);

  wire not_1_out, not_2_out, not_3_out;
  wire [3:0] xor_2_out;

  xor xor_1 (xor_2_out[0], Load[0], Increment);
  xor xor_2 (xor_2_out[1], Load[1], not_1_out);
  not not_1 (not_1_out, xor_2_out[0]);
  xor xor_3 (xor_2_out[2], Load[2], not_2_out);
  not not_2 (not_2_out, xor_2_out[1]);
  xor xor_4 (xor_2_out[3], Load[3], not_3_out);
  not not_3 (not_3_out, xor_2_out[2]);
  _4_bit_register _4_bit_register_1 (.Data(xor_2_out), .C(Increment), .Out(Address_bus));
endmodule
