// Digital circuit registerFile.dig as structural Verilog
module registerFile (
  input  [1:0] Control,
  input  [3:0] Data,
  input  R_W,
  input  Clear,
  output [3:0] DataOut
);

  wire not_1_out, not_2_out, not_3_out, not_4_out, or_1_out;
  wire [3:0] A_out, and_5_out, and_6_out, and_7_out, and_8_out, and_9_out, and_10_out, and_11_out,
       and_12_out, B_out, IR_out, not_5_out, xor_1_out;
  wire [3:3] and_1_out, and_2_out, and_3_out, and_4_out;

  and and_1 (and_1_out[3], not_1_out, not_2_out);
  not not_1 (not_1_out, Control[0]);
  not not_2 (not_2_out, Control[1]);
  and and_2 (and_2_out[3], Control[0], not_3_out);
  not not_3 (not_3_out, Control[1]);
  and and_3 (and_3_out[3], not_4_out, Control[1]);
  not not_4 (not_4_out, Control[0]);
  and and_4 (and_4_out[3], Control[0], Control[1]);
  assign not_5_out = ~{4{Clear}};  // Not not_5, 4 bits wide
  assign and_5_out = not_5_out & Data;  // And and_5, 4 bits wide
  assign and_6_out = and_5_out & {4{and_1_out[3]}};  // And and_6, 4 bits wide
  assign and_7_out = and_5_out & {4{and_2_out[3]}};  // And and_7, 4 bits wide
  assign and_8_out = and_5_out & {4{and_3_out[3]}};  // And and_8, 4 bits wide
  assign and_9_out = and_5_out & {4{and_4_out[3]}};  // And and_9, 4 bits wide
  assign xor_1_out = and_8_out ^ and_9_out;  // XOr xor_1, 4 bits wide
  or or_1 (or_1_out, R_W, Clear);
  _4_bit_register A (.Data(and_6_out), .C(or_1_out), .Out(A_out));
  _4_bit_register B (.Data(and_7_out), .C(or_1_out), .Out(B_out));
  _4_bit_register IR (.Data(xor_1_out), .C(or_1_out), .Out(IR_out));
  assign and_10_out = A_out & {4{and_1_out[3]}};  // And and_10, 4 bits wide
  assign and_11_out = B_out & {4{and_2_out[3]}};  // And and_11, 4 bits wide
  assign and_12_out = IR_out & {4{and_3_out[3]}};  // And and_12, 4 bits wide
  assign DataOut = and_10_out ^ and_11_out ^ and_12_out;  // XOr xor_2, 4 bits wide
endmodule
